# Fritzing sketch looplaunch (saved by Fritzing 0.9.3b)
breadboards: 2

parts:
  Teensy_3_1 = Teensy 3.1
  S1A = Pushbutton [package="[THT]"]
  S2B = Pushbutton [package="[THT]"]
  S3C = Pushbutton [package="[THT]"]
  S4D = Pushbutton [package="[THT]"]
  S5E = Pushbutton [package="[THT]"]
  S6F = Pushbutton [package="[THT]"]
  DIN1 = DIN-5 jack (MIDI) [package=THT]  # not connected
  S7Stop = Pushbutton [package="[THT]"]
  S8Prev = Pushbutton [package="[THT]"]
  S9Next = Pushbutton [package="[THT]"]
  TRS2 = Audio Jack (TRS) 3.5mm [package="4Ucon 08780 [THT]"]
  TRS3 = Audio Jack (TRS) 3.5mm [package="4Ucon 08780 [THT]"]
  Part1 = 0.56" 7-segment LED Backpack [part_number=878]

nets:
  GND: Teensy_3_1.GND, S1A.Pin_1, S1A.Pin_2, S2B.Pin_1, S2B.Pin_2, S3C.Pin_1, S3C.Pin_2, S4D.Pin_1, S4D.Pin_2, S5E.Pin_1, S5E.Pin_2, S6F.Pin_1, S6F.Pin_2, S7Stop.Pin_1, S7Stop.Pin_2, S8Prev.Pin_1, S8Prev.Pin_2, S9Next.Pin_1, S9Next.Pin_2, TRS2.Sleeve, TRS3.Sleeve, Part1.GND
  N1: Teensy_3_1.D4, S9Next.Pin_3, S9Next.Pin_4
  N2: Teensy_3_1.D5, S8Prev.Pin_3, S8Prev.Pin_4
  N3: Teensy_3_1.D6, S7Stop.Pin_3, S7Stop.Pin_4
  N4: Teensy_3_1.D7, S1A.Pin_3, S1A.Pin_4
  N5: Teensy_3_1.D8, S2B.Pin_3, S2B.Pin_4
  N6: Teensy_3_1.D9, S3C.Pin_3, S3C.Pin_4
  N7: Teensy_3_1.D10, S4D.Pin_3, S4D.Pin_4
  N8: Teensy_3_1.D11, S5E.Pin_3, S5E.Pin_4
  N9: Teensy_3_1.D12, S6F.Pin_3, S6F.Pin_4
  N10: Teensy_3_1.A0/D14, TRS2.Tip
  N11: Teensy_3_1.A1/D15, TRS2.Ring
  N12: Teensy_3_1.A2/D16, TRS3.Tip
  N13: Teensy_3_1.A3/D17, TRS3.Ring
  N14: Teensy_3_1.A4/D18, Part1.SDA
  N15: Teensy_3_1.A5/D19, Part1.SCL
  3V3: Teensy_3_1.3V3, Part1.VDD

custom parts:
  0.56" 7-segment LED Backpack: This 0.56" 7-segment LED display includes a driver chip for simple control via an I2C interface. The backpack features address-selection jumpers so you can connect up to eight displays on a single I2C bus.
